# Fritzing sketch peage-pay-simulation (saved by Fritzing 0.9.5d)
breadboards: 1

parts:
  Lecteur_RFID = RFID-RC522-v2
  R1 = Resistor [tolerance=±5% resistance=220 package="1206 [SMD]"]
  M1 = Dagu DGServo 9g (Top view) [part_number=RS001B]
  part = Arduino Nano (Rev3.0) (ICSP)
  LED5 = LED - 5mm [color="Blue (470nm)" package="5 mm [THT]"]
  SG1 = Buzzer 12mm [package=buzzer-12mm-ns]
  VCC1 = 4 x AAA Battery Mount
  LED6 = LED - 5mm [color="Green (555nm)" package="5 mm [THT]"]
  LED7 = LED - 5mm [color="Red (633nm)" package="5 mm [THT]"]
  R2 = Resistor [tolerance=±5% resistance=220 package="1206 [SMD]"]
  R3 = Resistor [tolerance=±5% resistance=220 package="1206 [SMD]"]

nets:
  N1: Lecteur_RFID.SDA, part.D10
  N2: Lecteur_RFID.SCK, part.D13/SCK
  N3: Lecteur_RFID.MOSI, part.D11/MOSI
  N4: Lecteur_RFID.MISO, part.D12/MISO
  GND: Lecteur_RFID.GND, M1.gnd, part.GND, LED5.cathode, SG1.2, VCC1.-, LED6.cathode, LED7.cathode
  N5: Lecteur_RFID.RST, part.D9
  N6: Lecteur_RFID.3_3V, part.3V3
  N7: R1.Pin_0, LED7.anode
  N8: R1.Pin_1, part.D4
  N9: M1.vcc, VCC1.+
  N10: M1.pulse, part.D3
  N11: part.D2, SG1.1
  N12: part.D5, R2.Pin_1
  N13: part.D6, R3.Pin_1
  N14: LED5.anode, R3.Pin_0
  N15: LED6.anode, R2.Pin_0

custom parts:
  RFID-RC522-v2: A simple China made RFID-RC522 Reader; do check the pin labels, as this is a MFRC522 based clone.
